# Fritzing sketch Schematic (saved by Fritzing 0.9.3b)
breadboards: 1

parts:
  Part1 = FTDI Basic Programmer
  U1 = atmega328 [package=dip]
  T1 = LM34 Temperature Sensor [package="TO92 [THT]"]

nets:
  N1: Part1.RXI, U1.D1_(TX)
  N2: Part1.TXO, U1.D0_(RX)
  N3: Part1.POWER, U1.VCC, U1.AVCC, U1.AREF, T1.+Vs
  GND: Part1.GND, U1.GND, T1.GND
  N4: U1.A0, T1.Vout
